# Fritzing sketch breadboard (saved by Fritzing 0.9.6b)
breadboards: 3

parts:
  U2 = 555 Timer [package="DIP8 [THT]"]
  R1 = Resistor [tolerance=±5% resistance=10k package="2512 [SMD]"]
  S1 = Pushbutton [package="[SMD]"]
  R2 = Resistor [tolerance=±5% resistance=10k package="2512 [SMD]"]
  S2 = Pushbutton [package="[SMD]"]
  U3 = 555 Timer [package="DIP8 [THT]"]
  LED1 = LED - 5mm [color="Red (633nm)" current=0.030 package="5 mm [THT]"]
  R3 = Resistor [tolerance=±5% resistance=470 package="2512 [SMD]"]  # not connected
  R5 = Resistor [tolerance=±5% resistance=100k package=THT]
  R6 = Resistor [tolerance=±5% resistance=100k power=0.25 package=THT]
  C1 = Capacitor [package=cap-pth-small2]
  C2 = Capacitor [package=cap-pth-small2]
  U4 = CD4026B [package=dil16]
  U6 = 7-SEGMENT-DISPLAY [package=7-segment-display]  # not connected
  R7 = Resistor [tolerance=±5% resistance=10k package="2512 [SMD]"]
  S3 = Pushbutton [package="[SMD]"]
  U7 = CD4026B [package=dil16]
  U8 = CD4026B [package=dil16]  # not connected
  U9 = 7-SEGMENT-DISPLAY [package=7-segment-display]  # not connected
  R8 = Resistor [tolerance=±5% resistance=10k package="2512 [SMD]"]

nets:
  N1: U2.Ground, U3.Ground, U3.Reset, U4.Y2, U4.Y3, U7.VEE
  N2: U2.Trigger, R1.Pin_1, S1.Pin_3, S1.Pin_4
  N3: U2.Output, U3.Vcc_Supply_Voltage, R5.Pin_0
  N4: U2.Reset, R2.Pin_1, S2.Pin_3, S2.Pin_4
  N5: U2.Threshold, LED1.anode, C1.2, C2.2, U4.X1, U7.B, U7.X1, R8.Pin_0
  N6: U2.Vcc_Supply_Voltage, U4.VCC, U7.X3
  N7: R1.Pin_0, R2.Pin_0, U4.Y, U7.GND
  N8: S1.Pin_1, S1.Pin_2, S2.Pin_1, S2.Pin_2
  N9: U3.Trigger, U3.Threshold, R6.Pin_0, C1.1
  N10: U3.Output, U4.Y0
  N11: U3.Control_Voltage, C2.1
  N12: U3.Discharge, R5.Pin_1
  N13: U4.X2, R7.Pin_1, S3.Pin_3, S3.Pin_4, U7.A, R8.Pin_1
  N14: S3.Pin_1, S3.Pin_2

custom parts:
  CD4026B: Dual 4:1 analog mux
